# Fritzing sketch sketch (saved by Fritzing 0.9.3b)

parts:
  Part1 = Adafruit MAX31865 RTD Sensor Breakout [part_number="Adafruit #3328"]
  Raspberry_Pi_Zero1 = Raspberry Pi Zero
  MPX4250AP1 = MPX4250AP pressure sensor2 [part_number=MPX]
  Part2 = BluePill
  Part3 = Adafruit MAX31865 RTD Sensor Breakout [part_number="Adafruit #3328"]
  Part4 = Adafruit MAX31865 RTD Sensor Breakout [part_number="Adafruit #3328"]
  Part5 = Adafruit MAX31865 RTD Sensor Breakout [part_number="Adafruit #3328"]
  Part6 = Adafruit MAX31865 RTD Sensor Breakout [part_number="Adafruit #3328"]
  MPX4250AP2 = MPX4250AP pressure sensor2 [part_number=MPX]
  MPX4250AP3 = MPX4250AP pressure sensor2 [part_number=MPX]
  MPX4250AP4 = MPX4250AP pressure sensor2 [part_number=MPX]
  MPX4250AP5 = MPX4250AP pressure sensor2 [part_number=MPX]
  MPX4250AP6 = MPX4250AP pressure sensor2 [part_number=MPX]

nets:
  VIN: Part1.VIN, Raspberry_Pi_Zero1.5V, MPX4250AP1.Vs, Part2.5V, Part3.VIN, Part4.VIN, Part5.VIN, Part6.VIN, MPX4250AP2.Vs, MPX4250AP3.Vs, MPX4250AP4.Vs, MPX4250AP5.Vs, MPX4250AP6.Vs
  GND: Part1.GND, Raspberry_Pi_Zero1.GND, Part2.GND3, Part3.GND, Part4.GND, Part5.GND, Part6.GND
  N1: Part1.SCLK, Part2.A5, Part3.SCLK, Part4.SCLK, Part5.SCLK, Part6.SCLK
  N2: Part1.SDO, Part2.A6, Part3.SDO, Part4.SDO, Part5.SDO, Part6.SDO
  N3: Part1.SDI, Part2.A7, Part3.SDI, Part4.SDI, Part5.SDI, Part6.SDI
  N4: Part1.CS, Part2.B7
  N5: Raspberry_Pi_Zero1.GPIO15, Part2.A9
  N6: Raspberry_Pi_Zero1.GPIO14, Part2.A10
  N7: MPX4250AP1.V_out, Part2.B0
  GND_2: MPX4250AP1.GND, Part2.GND, Part2.GND2, MPX4250AP2.GND, MPX4250AP3.GND, MPX4250AP4.GND, MPX4250AP5.GND, MPX4250AP6.GND
  N8: Part2.A0, MPX4250AP6.V_out
  N9: Part2.A1, MPX4250AP5.V_out
  N10: Part2.A3, MPX4250AP3.V_out
  N11: Part2.A4, MPX4250AP2.V_out
  N12: Part2.B6, Part3.CS
  N13: Part2.B5, Part4.CS
  N14: Part2.B4, Part5.CS
  N15: Part2.B3, Part6.CS
  N16: Part2.A2, MPX4250AP4.V_out

notes:
  UART
  SPI
  ADC

custom parts:
  Adafruit MAX31865 RTD Sensor Breakout: For precision temperature sensing, nothing beats a Platinum RTD. Resistance temperature detectors (RTDs) are temperature sensors that contain a resistor that changes resistance value as its temperature changes, basically a kind of thermistor. In this sensor, the resistor is actually a small strip of Platinum with a resistance of 100 ohms at 0°C, thus the name PT100. Compared to most NTC/PTC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
  MPX4250AP pressure sensor2: MPX4250AP - MPX4250A SERIES Motorola Preferred Device ORIGINAL MANUFACTURER MOUNTING - flat side up Integrated Silicon Pressure Sensor Manifold Absolute Pressure Sensor On-Chip Signal Conditioned, Temperature Compensated and Calibrated The MPX4250A series piezoresistive transducer is a state-of-the-art monolithic silicon pressure sensor designed for a wide range of applications, particularly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
