# Fritzing sketch sketch (saved by Fritzing 0.9.3b)

parts:
  YF-S201_Flow_Meter1 = YF-S201 Water Flow Meter
  Part1 = Arduino Mega 2560 (Rev3)
  U1 = ESP8266 NodeMCU LoLin module
  R1 = Resistor [tolerance=±5% resistance=220 package="0805 [SMD]"]
  R2 = Resistor [tolerance=±5% resistance=220 package="0805 [SMD]"]
  R3 = Resistor [tolerance=±5% resistance=220 package="0805 [SMD]"]
  U3 = SWITCH-SPST-2 [package=switch-spst-vertical]
  BAT1 = 12 battery [package=battery]
  BAT2 = 12 battery [package=battery]
  Reg1 = DC-DC CONVERTER [part_number=80633 package=dc-dc_converter]
  Part2 = Solar Cell
  Mod1 = Solar Charge Controller [part_number="KLD Series Solar Charge Controller PWM" package=PWM-Model]
  F1 = Fan - Ventilador [package=THT]
  Part3 = Solar Cell
  Part4 = Solar Cell
  U4 = 2-Channel 5v Relay Shield [package=relay-2ch5v10a]
  J1 = Piezo Speaker

nets:
  N1: YF-S201_Flow_Meter1.SIG, Part1.D2_PWM, R1.Pin_0
  GND: YF-S201_Flow_Meter1.GND, Part1.GND, U1.GND, R3.Pin_0, Reg1.OUT-, U4.GND
  VCC: YF-S201_Flow_Meter1.VCC, Part1.5V, U1.Vin, R1.Pin_1, U4.VCC
  N2: Part1.D19/RX1, U1.TX
  N3: Part1.D18/TX1, R2.Pin_1
  N4: Part1.VIN, Reg1.OUT+
  N5: Part1.D3_PWM, U4.IN1
  N6: U1.RX, R2.Pin_0, R3.Pin_1
  N7: U3.O, Mod1.Connector_5
  N8: U3.P, Reg1.IN+, F1.5V, U4.K1-In
  N9: BAT1.-, BAT2.-, Mod1.Connector_4
  N10: BAT1.+, BAT2.+, Mod1.Connector_3
  N11: Reg1.IN-, Mod1.Connector_6, F1.GND, J1.pin1
  N12: Part2.+, Mod1.Connector_1, Part3.+, Part4.+
  N13: Part2.-, Mod1.Connector_2, Part3.-, Part4.-
  N14: U4.K1-Off, J1.pin2

notes:
  10k Ohm
  1k Ohm
  2k Ohm
  if data sent by Arduino can't be read by MCU, then remove the resistor and the pull down in TX (Arduino) to RX (MCU)
  12 VDC
  9 VDC
  Sinere 12 VDC

custom parts:
  YF-S201 Water Flow Meter: The YF-S201 Flow Meter. The input voltage is 5V to 24V (DC).
  ESP8266 NodeMCU LoLin module: ESP8266 based NodeMCU
  12 battery: 12V lead acid type battery, like the Husqvarna YTH2448 12V 35AH battery. This is the mini version 1/4 the size of the actual battery to be closer to typical breadboard parts (around 2in wide rathher than 7in). The pads in pcb are sized to accomidate up to 14ga wire (as these batterys will deliver high currents.)
  DC-DC CONVERTER: WYHP 5A constant current/voltage manufactured by Shenzhen Weiyapuhua Technology Co., Ltd
  Solar Charge Controller: PWM-Solar Charge Controller
  Fan - Ventilador: Ventilador de 2 pines, se encuentra comunmente en computadoras de escritorio
  2-Channel 5v Relay Shield: 2 Channel 5v Relay Shield w. 2x SPD-06VDC-SD-C
